# Fritzing sketch mycircuit (saved by Fritzing 0.9.3b)

parts:
  Maker_/_Arduino_Uno = Maker Uno (Arduino Uno Compatible)
  Bluetooth_HC-05 = Bluetooth HC-05 Macho
  Analog_Joystick = Black Joystick KY-023

nets:
  N1: Maker_/_Arduino_Uno.A0, Analog_Joystick.VRx
  N2: Maker_/_Arduino_Uno.A1, Analog_Joystick.VRy
  GND: Maker_/_Arduino_Uno.GND, Bluetooth_HC-05.GND, Analog_Joystick.GND
  N3: Maker_/_Arduino_Uno.D2, Bluetooth_HC-05.TXD
  N4: Maker_/_Arduino_Uno.D3_PWM, Bluetooth_HC-05.RXD
  5V: Maker_/_Arduino_Uno.5V, Bluetooth_HC-05.VCC, Analog_Joystick.+5V

notes:
  ⬆️ This side up ⬆️
  State & Key pin not connected

custom parts:
  Maker Uno (Arduino Uno Compatible): Maker Uno, an Arduino UNO compatible board designed and developed specially for students to learn coding and microcontroller. We named it Maker UNO to encourage everyone to be a maker by getting started with this amazing board. Oh! BTW, it is PURPLE color.
  Black Joystick KY-023: Description: The joystick is a combination of 2 analoog potentiometer and a digital switch. Arduino GND --> Module pin - Arduino +5V --> Module pin +5V Arduino Analoog 0 --> Module VRx Arduino Analoog 1 --> Module VRy Arduino Digital --> Module SW Dimensions: 1" x 1.25"
